# Fritzing sketch part1a (saved by Fritzing 0.9.2b)

parts:
  Part1 = Arduino Uno (Rev3)
  S1 = H-Bridge with L298N
  BAT1 = BC9VPC [package=bc9vpc]
  M1 = DC Motor

nets:
  N1: Part1.D3_PWM, S1.IN1
  GND: Part1.GND, S1.GND, BAT1.V-
  N2: S1.12V, BAT1.V+
  N3: S1.ENA, S1.ENA-5V
  N4: S1.M1-01, M1.pin_2
  N5: S1.M1-02, M1.pin_1

notes:
  Part 1a
  TWO PWM PINS USED For Speed and Direction Control
  ENABLE PIN ON.

custom parts:
  H-Bridge with L298N: h-bridge
