# Fritzing sketch part3 and 4 (saved by Fritzing 0.9.2b)

parts:
  Part1 = Arduino Uno (Rev3)
  S1 = H-Bridge with L298N
  BAT1 = BC9VPC [package=bc9vpc]
  M1 = DC Motor

nets:
  N1: Part1.D5_PWM, S1.IN2
  GND: Part1.GND, S1.GND, BAT1.V-
  N2: S1.12V, BAT1.V+
  N3: S1.M1-01, M1.pin_2
  N4: S1.M1-02, M1.pin_1

notes:
  Part 3 and Part 4
  Wire Diagram is Same for both Sketches. Part 3 Uses NO PWM, Part 4 Uses One PWM on Connected to the ENABLE PIN

custom parts:
  H-Bridge with L298N: h-bridge
