# Fritzing sketch part5 (saved by Fritzing 0.9.2b)

parts:
  Part1 = Arduino Uno (Rev3)
  S1 = H-Bridge with L298N
  BAT1 = BC9VPC [package=bc9vpc]
  M1 = DC Motor

nets:
  GND: Part1.GND, S1.GND, BAT1.V-
  N1: S1.12V, BAT1.V+
  N2: S1.M1-01, M1.pin_2
  N3: S1.M1-02, M1.pin_1

notes:
  Part 5 uses Inverted Logic for Speed and Direction control plus Enable Pins.

custom parts:
  H-Bridge with L298N: h-bridge
