# Fritzing sketch switch interrupt (saved by Fritzing 0.9.2b)

parts:
  Part1 = Arduino Uno (Rev3)
  S1 = H-Bridge with L298N
  BAT1 = BC9VPC [package=bc9vpc]
  M1 = DC Motor
  S2 = SWITCH-MOMENTARY-2 [package=tactile_switch_tall]

nets:
  N1: Part1.D2, S2.2
  N2: Part1.D5_PWM, S1.ENA
  GND: Part1.GND, S1.GND, BAT1.V-
  N3: S1.12V, BAT1.V+
  N4: S1.M1-01, M1.pin_2
  N5: S1.M1-02, M1.pin_1

notes:
  A switch can also be used on the interrupt pin, and software can be used as a emerancy cut off, or safety switch

custom parts:
  H-Bridge with L298N: h-bridge
