# Fritzing sketch switched enable (saved by Fritzing 0.9.2b)

parts:
  Part1 = Arduino Uno (Rev3)
  S1 = H-Bridge with L298N
  BAT1 = BC9VPC [package=bc9vpc]
  M1 = DC Motor
  S2 = SWITCH-MOMENTARY-2 [package=tactile_switch_tall]

nets:
  GND: Part1.GND, S1.GND, BAT1.V-
  N1: S1.12V, BAT1.V+
  N2: S1.ENA, S2.1
  N3: S1.M1-01, M1.pin_2
  N4: S1.M1-02, M1.pin_1

notes:
  A Normally Closed switch can be used on the ENABLE pin, to act as a safety, or emergancy cut off of the motors. Just about any type of switch can be used here. This is just a representation.

custom parts:
  H-Bridge with L298N: h-bridge
